# Fritzing sketch ButtonLED (saved by Fritzing 0.9.3b)
breadboards: 1

parts:
  Componente1 = Arduino Uno (Rev3)
  S1 = Round Pushbutton
  LED1 = LEDs [package=led10mm]
  R1 = Resistor [tolerance=±5% resistance=1k package=THT]

nets:
  N1: Componente1.D2, S1.leg1, R1.Pin_0
  N2: Componente1.D4, LED1.C
  N3: Componente1.5V, S1.leg0
  N4: Componente1.GND, LED1.A, R1.Pin_1
