# Fritzing sketch SchemaBottoni (saved by Fritzing 0.9.3b)
breadboards: 3

parts:
  Componente2 = Arduino Mega 2560 (Rev3)
  S2 = Round Pushbutton
  S3 = Round Pushbutton
  S4 = Round Pushbutton
  S5 = Round Pushbutton
  S6 = Round Pushbutton
  S7 = Round Pushbutton
  S8 = Round Pushbutton
  S9 = Round Pushbutton
  S10 = Round Pushbutton
  S11 = Round Pushbutton
  S12 = Round Pushbutton
  S13 = Round Pushbutton
  R2 = Resistor [tolerance=±5% resistance=1k package=THT]
  R3 = Resistor [tolerance=±5% resistance=1k package=THT]
  R4 = Resistor [tolerance=±5% resistance=1k package=THT]
  R5 = Resistor [tolerance=±5% resistance=1k package=THT]
  R7 = Resistor [tolerance=±5% resistance=1k package=THT]
  R8 = Resistor [tolerance=±5% resistance=1k package=THT]
  R9 = Resistor [tolerance=±5% resistance=1k package=THT]
  R10 = Resistor [tolerance=±5% resistance=1k package=THT]
  R11 = Resistor [tolerance=±5% resistance=1k package=THT]
  R12 = Resistor [tolerance=±5% resistance=1k package=THT]
  R13 = Resistor [tolerance=±5% resistance=1k package=THT]
  R14 = Resistor [tolerance=±5% resistance=1k package=THT]

nets:
  N1: Componente2.GND, R2.Pin_0, R3.Pin_0, R4.Pin_0, R5.Pin_1, R7.Pin_0, R8.Pin_0, R9.Pin_0, R10.Pin_0, R11.Pin_0, R12.Pin_0, R13.Pin_0, R14.Pin_0
  N2: Componente2.5V, S2.leg0, S3.leg0, S4.leg0, S5.leg0, S6.leg0, S7.leg0, S8.leg0, S9.leg0, S10.leg0, S11.leg0, S12.leg0, S13.leg0
  N3: Componente2.D22, S12.leg1, R7.Pin_1
  N4: Componente2.D24, S13.leg1, R9.Pin_1
  N5: Componente2.D26, S9.leg1, R11.Pin_1
  N6: Componente2.D28, S8.leg1, R12.Pin_1
  N7: Componente2.D30, S3.leg1, R10.Pin_1
  N8: Componente2.D32, S10.leg1, R13.Pin_1
  N9: Componente2.D34, S5.leg1, R5.Pin_0
  N10: Componente2.D36, S7.leg1, R4.Pin_1
  N11: Componente2.D38, S6.leg1, R3.Pin_1
  N12: Componente2.D40, S2.leg1, R2.Pin_1
  N13: Componente2.D42, S11.leg1, R8.Pin_1
  N14: Componente2.D44, S4.leg1, R14.Pin_1
