# Fritzing sketch SchemaLED (saved by Fritzing 0.9.3b)
breadboards: 3

parts:
  LED1 = LED - 5mm [color="Red (633nm)" package="5 mm [THT]"]
  LED2 = LED - 5mm [color="Red (633nm)" package="5 mm [THT]"]
  LED3 = LED - 5mm [color="Red (633nm)" package="5 mm [THT]"]
  LED4 = LED - 5mm [color="Red (633nm)" package="5 mm [THT]"]
  LED5 = LED - 5mm [color="Red (633nm)" package="5 mm [THT]"]
  LED6 = LED - 5mm [color="Red (633nm)" package="5 mm [THT]"]
  LED7 = LED - 5mm [color="Red (633nm)" package="5 mm [THT]"]
  LED8 = LED - 5mm [color="Red (633nm)" package="5 mm [THT]"]
  LED9 = LED - 5mm [color="Red (633nm)" package="5 mm [THT]"]
  LED10 = LED - 5mm [color="Red (633nm)" package="5 mm [THT]"]
  LED11 = LED - 5mm [color="Red (633nm)" package="5 mm [THT]"]
  LED12 = LED - 5mm [color="Red (633nm)" package="5 mm [THT]"]
  Componente1 = Arduino Mega 2560 (Rev3)

nets:
  N1: LED1.cathode, LED2.cathode, LED3.cathode, LED4.cathode, LED5.cathode, LED6.cathode, LED7.cathode, LED8.cathode, LED9.cathode, LED10.cathode, LED11.cathode, LED12.cathode, Componente1.GND
  N2: LED1.anode, Componente1.D41
  N3: LED2.anode, Componente1.D39
  N4: LED3.anode, Componente1.D25
  N5: LED4.anode, Componente1.D23
  N6: LED5.anode, Componente1.D33
  N7: LED6.anode, Componente1.D31
  N8: LED7.anode, Componente1.D29
  N9: LED8.anode, Componente1.D43
  N10: LED9.anode, Componente1.D27
  N11: LED10.anode, Componente1.D45
  N12: LED11.anode, Componente1.D35
  N13: LED12.anode, Componente1.D37
